// Digital circuit MUX.dig as structural Verilog
module MUX (
  input  D,
  input  C,
  input  B,
  input  A,
  output Y
);

  // Not not_1 is placed but not wired
  Multiplexer #(.Selector_Bits(3)) multiplexer_1 (
    .sel({C, A, D}), .in_1(1'b0), .in_2(1'b1), .in_3(1'b1), .in_4(1'b0), .out(Y));  // open: in_0, in_5, in_6, in_7

  // Notes on the sheet:
  //   Use A as the most-significant bit and 
  //   D as the least-significant bit.
  //   Converts between single bits & a 3-bit bus
endmodule

/* Test case:
A B C D Y
0 0 0 0 X
0 0 0 1 1
*/
