// Digital circuit MUX_74151.dig as structural Verilog
module MUX_74151 (
  input  D,
  input  C,
  input  B,
  input  A,
  output Y
);

  wire _74151_1_pin13, not_1_out;

  not not_1 (not_1_out, _74151_1_pin13);
  _74151 _74151_1 (
    .pin5(Y), .pin7(1'b0), .pin8(1'b0), .pin12(D), .pin13(_74151_1_pin13), .pin14(D), .pin15(not_1_out),
    .pin16(1'b1));  // open: pin1, pin2, pin3, pin4, pin6, pin9, pin10, pin11
  // Not not_2 has open pins: in=open, out=D

  // Notes on the sheet:
  //   74151 Multiplexer:
  //   C,B,A are select bits.  C is the MSB.
  //   D0-D7 are input data lines
  //   Y is the output
  //   W is the inverted output
  //   S is strobe.  When strobe is high the output is always low, 
  //     otherwise it's the selected data line.
  //   Inputs: Use A as the most-significant bit and 
  //   D as the least-significant bit.
endmodule

/* Test case:
A B C D Y
0 0 0 0 X
0 0 0 1 1
*/
